// Logisim project 10-2-Adder1bit.circ as structural Verilog: 1 circuit, main circuit main
module main (
  input  A,
  input  B,
  input  R,
  output Resultat,
  output Retenue
);

  wire and_1_out, and_2_out, and_3_out, and_4_out, and_5_out, and_6_out, and_7_out, not_1_out, not_2_out,
       not_3_out, not_4_out, not_5_out, not_6_out, not_7_out, not_8_out;

  not not_1 (not_1_out, A);
  not not_2 (not_2_out, B);
  not not_3 (not_3_out, A);
  and and_1 (and_1_out, not_3_out, not_4_out, R);
  not not_4 (not_4_out, B);
  not not_5 (not_5_out, A);
  and and_2 (and_2_out, not_5_out, B, not_6_out);
  not not_6 (not_6_out, R);
  and and_3 (and_3_out, A, not_7_out, not_8_out);
  not not_7 (not_7_out, B);
  not not_8 (not_8_out, R);
  and and_4 (and_4_out, A, B, R);
  and and_5 (and_5_out, not_1_out, B, R);
  and and_6 (and_6_out, A, not_2_out, R);
  and and_7 (and_7_out, A, B);
  or or_1 (Resultat, and_1_out, and_2_out, and_3_out, and_4_out);
  or or_2 (Retenue, and_5_out, and_6_out, and_7_out);

  // Notes on the sheet:
  //   Retenue(A,B,R) = (non(A) et B et R) ou (A et non(B) et R) ou (A et B)
  //   Resultat(A,B,R) =  (non(A) et non(B) et R) ou (non(A) et B et non(R)) ou (A et non(B) et non(R)) ou (A et B et R)
endmodule
